// Logisim project Components.circ as structural Verilog: 14 circuits, main circuit Instruction Decoder
module Control_Unit (
  input  in_1,
  input  [5:0] in_2,
  input  in_3,
  input  [5:0] in_4,
  input  in_5,
  input  [3:0] in_6,
  input  in_7,
  input  [3:0] in_8,
  input  in_9,
  input  in_10,
  input  in_11,
  output out_12,
  output out_13,
  output out_14,
  output out_15,
  output [1:0] out_16,
  output out_17,
  output out_18,
  output [1:0] out_19,
  output out_20,
  output out_21,
  output [1:0] out_22,
  output out_23,
  output out_24,
  output [1:0] out_25,
  output out_26,
  output out_27,
  output [2:0] out_28,
  output out_29,
  output out_30,
  output [3:0] out_31,
  output out_32,
  output out_33,
  output out_34
);

  wire AdrSrc_0a, AdrSrc_1a, AdrSrc_1b, ALUCalc_0a, ALUCalc_0b, ALUCalc_0c, ALUSrcB_1a, and_1_out, and_2_out,
       and_3_out, Arit, Arit_End, Arit_I, Arit_I_End, Cache_En__0, Cache_En__1, comparator_1_eq,
       comparator_2_gt, comparator_3_lt, Copia, Copia_End, CS_1, CS_2, CS_3, CS_6, CS_8, d_ff_2_q, d_ff_16_q,
       DA_Slc_0a, DA_Slc_0b, DA_Slc_1a, Data_Slc_0a, Data_Slc_0b, Data_Slc_0d, Decoded_q,
       demultiplexer_1_out0, demultiplexer_1_out1, demultiplexer_2_out0, demultiplexer_2_out1,
       demultiplexer_3_out1, demultiplexer_5_out1, demultiplexer_6_out0, demultiplexer_7_out0,
       demultiplexer_7_out1, demultiplexer_8_out0, demultiplexer_9_out0, demultiplexer_9_out1,
       demultiplexer_10_out0, demultiplexer_10_out1, demultiplexer_11_out0, demultiplexer_12_out0,
       demultiplexer_12_out1, demultiplexer_14_out0, demultiplexer_15_out0, demultiplexer_16_out0,
       demultiplexer_16_out1, End_Read, End_Write, Especial, Especial_End, EWC, Fetch_Instr_q, halt,
       IDLE_2_q, IDLE_q, Lw, Lw_End, not_1_out, or_3_out, or_4_out, or_6_out, or_8_out, or_10_out, or_11_out,
       or_12_out, or_13_out, or_14_out, or_15_out, or_16_out, or_24_out, or_28_out, PCEn_3, PCEn_5, PCEn_7,
       Pila, R_W_1, ResultLoad_1, rnd, Salto, Salto_End, Start, Sw, temp_1_out_4, temp_2_out_4, temp_3_out_4,
       Timer_Reset;
  wire [1:0] ALUCalc;
  wire [2:0] Demul_S;
  wire [3:0] ALU_S;

  or or_1 (CS_8, demultiplexer_1_out0, Start);
  D_Flip_Flop #(.trigger("falling")) Copy (.clk(in_1), .D(Copia), .Q(out_28[1]), .reset(in_3));  // open: Qn, preset, en
  Comparator #(.width(6)) comparator_1 (.a(in_4), .b(6'b010000), .eq(comparator_1_eq));  // open: gt, lt
  D_Flip_Flop #(.trigger("falling")) Calculate (
    .clk(in_1), .D(Lw), .Q(ALUCalc_0b), .reset(in_3));  // open: Qn, preset, en
  D_Flip_Flop #(.trigger("falling")) d_ff_1 (.clk(in_1), .D(Sw), .Q(ALUCalc_0c), .reset(in_3));  // open: Qn, preset, en
  D_Flip_Flop #(.trigger("falling")) d_ff_2 (
    .clk(in_1), .D(Especial), .Q(d_ff_2_q), .reset(in_3));  // open: Qn, preset, en
  not not_1 (not_1_out, out_12);
  D_Flip_Flop #(.trigger("falling")) IDLE (.clk(in_1), .D(CS_8), .Q(IDLE_q), .reset(in_3));  // open: Qn, preset, en
  Demultiplexer #(.enable("false")) demultiplexer_1 (
    .out0(demultiplexer_1_out0), .out1(demultiplexer_1_out1), .in(IDLE_q), .sel(not_1_out));
  D_Flip_Flop #(.trigger("falling")) IDLE_2 (
    .clk(in_1), .D(demultiplexer_2_out1), .Q(IDLE_2_q), .preset(in_3));  // open: Qn, en, reset
  Demultiplexer #(.enable("false")) demultiplexer_2 (
    .out0(demultiplexer_2_out0), .out1(demultiplexer_2_out1), .in(IDLE_2_q), .sel(in_3));
  Demultiplexer #(.enable("false")) demultiplexer_3 (
    .out0(Data_Slc_0a), .out1(demultiplexer_3_out1), .in(out_28[1]), .sel(comparator_1_eq));
  Demultiplexer #(.select(2), .enable("false")) demultiplexer_4 (
    .out0(out_20), .out1(rnd), .out2(out_29), .out3(halt), .in(d_ff_2_q), .sel(in_4[2:1]));
  or or_2 (Timer_Reset, demultiplexer_1_out1, demultiplexer_2_out0);
  D_Flip_Flop #(.trigger("falling")) Calculate_2 (
    .clk(in_1), .D(Arit), .Q(ResultLoad_1), .reset(in_3));  // open: Qn, preset, en
  Comparator #(.width(6)) comparator_2 (.a(in_4), .b(6'b010111), .gt(comparator_2_gt));  // open: eq, lt
  Comparator #(.width(6)) comparator_3 (.a(in_4), .b(6'b011100), .lt(comparator_3_lt));  // open: gt, eq
  D_Flip_Flop #(.trigger("falling")) Calculate_3 (
    .clk(in_1), .D(Arit_I), .Q(ALUSrcB_1a), .reset(in_3));  // open: Qn, preset, en
  or or_3 (or_3_out, Data_Slc_0a, demultiplexer_3_out1);
  or or_4 (or_4_out, demultiplexer_9_out0, ALUCalc_0b);
  Demultiplexer #(.enable("false")) demultiplexer_5 (
    .out0(CS_2), .out1(demultiplexer_5_out1), .in(Pila), .sel(in_4[0]));
  or or_5 (CS_1, demultiplexer_8_out0, Timer_Reset);
  Demultiplexer #(.enable("false")) demultiplexer_6 (
    .out0(demultiplexer_6_out0), .out1(out_18), .in(ResultLoad_1), .sel(and_1_out));
  and and_1 (and_1_out, comparator_2_gt, comparator_3_lt);
  D_Flip_Flop #(.trigger("falling")) End (
    .clk(in_1), .D(or_3_out), .Q(Copia_End), .reset(in_3));  // open: Qn, preset, en
  or or_6 (or_6_out, demultiplexer_10_out0, ALUCalc_0c);
  or or_7 (out_28[2], rnd, out_29);
  or or_8 (or_8_out, out_23, halt);
  D_Flip_Flop #(.trigger("falling")) d_ff_3 (
    .clk(in_1), .D(demultiplexer_5_out1), .Q(ALUCalc[1]), .reset(in_3));  // open: Qn, preset, en
  or or_9 (EWC, out_24, ~in_5);  // OR_Gate
  D_Flip_Flop #(.trigger("falling")) Fetch_Instr (
    .clk(in_1), .D(CS_1), .Q(Fetch_Instr_q), .reset(in_3));  // open: Qn, preset, en
  D_Flip_Flop #(.trigger("falling")) Write_Reg (
    .clk(in_1), .D(ALUSrcB_1a), .Q(DA_Slc_0a), .reset(in_3));  // open: Qn, preset, en
  D_Flip_Flop #(.trigger("falling")) Read_RAM (
    .clk(in_1), .D(or_4_out), .Q(AdrSrc_0a), .reset(in_3));  // open: Qn, preset, en
  D_Flip_Flop #(.trigger("falling")) d_ff_4 (
    .clk(in_1), .D(or_6_out), .Q(out_26), .reset(in_3));  // open: Qn, preset, en
  D_Flip_Flop #(.trigger("falling")) d_ff_5 (
    .clk(in_1), .D(or_8_out), .Q(out_23), .reset(in_3));  // open: Qn, preset, en
  D_Flip_Flop #(.trigger("falling")) d_ff_6 (
    .clk(in_1), .D(or_10_out), .Q(AdrSrc_1a), .reset(in_3));  // open: Qn, preset, en
  or or_10 (or_10_out, demultiplexer_12_out0, CS_2);
  and and_2 (and_2_out, EWC, out_21);
  Demultiplexer #(.enable("false")) demultiplexer_7 (
    .out0(demultiplexer_7_out0), .out1(demultiplexer_7_out1), .in(and_2_out), .sel(in_7));
  Demultiplexer #(.enable("false")) demultiplexer_8 (
    .out0(demultiplexer_8_out0), .out1(out_32), .in(Fetch_Instr_q), .sel(temp_1_out_4));
  Temp temp_1 (.in_1(in_6), .out_4(temp_1_out_4), .CLK(in_1), .Clear(Timer_Reset));
  D_Flip_Flop #(.trigger("falling")) Write_Reg_2 (
    .clk(in_1), .D(demultiplexer_6_out0), .Q(R_W_1), .reset(in_3));  // open: Qn, preset, en
  Demultiplexer #(.enable("false")) demultiplexer_9 (
    .out0(demultiplexer_9_out0), .out1(demultiplexer_9_out1), .in(AdrSrc_0a), .sel(out_27));
  Demultiplexer #(.enable("false")) demultiplexer_10 (
    .out0(demultiplexer_10_out0), .out1(demultiplexer_10_out1), .in(out_26), .sel(End_Write));
  Demultiplexer #(.enable("false")) demultiplexer_11 (
    .out0(demultiplexer_11_out0), .out1(Data_Slc_0d), .in(out_28[2]), .sel(out_29));
  Demultiplexer #(.enable("false")) demultiplexer_12 (
    .out0(demultiplexer_12_out0), .out1(demultiplexer_12_out1), .in(AdrSrc_1a), .sel(out_27));
  and and_3 (and_3_out, ~out_24, demultiplexer_7_out0);  // AND_Gate
  or or_11 (or_11_out, demultiplexer_14_out0, demultiplexer_7_out1);
  D_Flip_Flop #(.trigger("falling")) Decoded (
    .clk(in_1), .D(out_32), .Q(Decoded_q), .reset(in_3));  // open: Qn, preset, en
  or or_12 (or_12_out, R_W_1, out_18);
  D_Flip_Flop #(.trigger("falling")) End_2 (
    .clk(in_1), .D(DA_Slc_0a), .Q(Arit_I_End), .reset(in_3));  // open: Qn, preset, en
  D_Flip_Flop #(.trigger("falling")) Write_Reg_3 (
    .clk(in_1), .D(demultiplexer_9_out1), .Q(DA_Slc_0b), .reset(in_3));  // open: Qn, preset, en
  or or_13 (or_13_out, demultiplexer_11_out0, Data_Slc_0d);
  D_Flip_Flop #(.trigger("falling")) d_ff_7 (
    .clk(in_1), .D(ALUCalc[1]), .Q(CS_3), .reset(in_3));  // open: Qn, preset, en
  or or_14 (or_14_out, demultiplexer_15_out0, and_3_out);
  D_Flip_Flop #(.trigger("falling")) d_ff_8 (
    .clk(in_1), .D(or_11_out), .Q(out_12), .reset(in_3));  // open: Qn, preset, en
  Demultiplexer #(.select(3), .enable("false")) demultiplexer_13 (
    .out0(Arit), .out1(Copia), .out2(Salto), .out3(Arit_I), .out4(Pila), .out5(Lw), .out6(Sw),
    .out7(Especial), .in(Decoded_q), .sel(Demul_S));
  D_Flip_Flop #(.trigger("falling")) End_3 (
    .clk(in_1), .D(or_12_out), .Q(Arit_End), .reset(in_3));  // open: Qn, preset, en
  D_Flip_Flop #(.trigger("falling")) Jump (.clk(in_1), .D(Salto), .Q(PCEn_3), .reset(in_3));  // open: Qn, preset, en
  D_Flip_Flop #(.trigger("falling")) d_ff_9 (
    .clk(in_1), .D(demultiplexer_10_out1), .Q(PCEn_7), .reset(in_3));  // open: Qn, preset, en
  D_Flip_Flop #(.trigger("falling")) d_ff_10 (
    .clk(in_1), .D(demultiplexer_12_out1), .Q(Data_Slc_0b), .reset(in_3));  // open: Qn, preset, en
  D_Flip_Flop #(.trigger("falling")) d_ff_11 (
    .clk(in_1), .D(or_14_out), .Q(CS_6), .reset(in_3));  // open: Qn, preset, en
  Demultiplexer #(.enable("false")) demultiplexer_14 (
    .out0(demultiplexer_14_out0), .out1(End_Write), .in(out_12), .sel(temp_2_out_4));
  Temp temp_2 (.in_1(in_8), .out_4(temp_2_out_4), .CLK(in_1), .Clear(Timer_Reset));
  Operation_Decoder operation_decoder_1 (
    .Inputs(in_2), .in_2(in_4), .in_3(in_9), .in_4(in_10), .in_5(in_11), .out_6(ALU_S), .out_7(Demul_S),
    .out_8(out_22), .out_9(out_33));
  D_Flip_Flop #(.trigger("falling")) d_ff_12 (
    .clk(in_1), .D(or_15_out), .Q(Especial_End), .reset(in_3));  // open: Qn, preset, en
  or or_15 (or_15_out, or_13_out, out_20);
  D_Flip_Flop #(.trigger("falling")) End_4 (.clk(in_1), .D(PCEn_3), .Q(Salto_End));  // open: Qn, preset, en, reset
  D_Flip_Flop #(.trigger("falling")) d_ff_13 (
    .clk(in_1), .D(Data_Slc_0b), .Q(ALUCalc_0a), .reset(in_3));  // open: Qn, preset, en
  Demultiplexer #(.enable("false")) demultiplexer_15 (
    .out0(demultiplexer_15_out0), .out1(End_Read), .in(CS_6), .sel(temp_3_out_4));
  Temp temp_3 (.in_1(in_6), .out_4(temp_3_out_4), .CLK(in_1), .Clear(Timer_Reset));
  D_Flip_Flop #(.trigger("falling")) End_5 (
    .clk(in_1), .D(DA_Slc_0b), .Q(Lw_End), .reset(in_3));  // open: Qn, preset, en
  or or_16 (or_16_out, demultiplexer_16_out0, CS_3);
  or or_17 (Start, Arit_End, Copia_End, Salto_End, Arit_I_End, PCEn_5, Lw_End, PCEn_7, Especial_End);
  D_Flip_Flop #(.trigger("falling")) d_ff_14 (
    .clk(in_1), .D(or_16_out), .Q(AdrSrc_1b), .reset(in_3));  // open: Qn, preset, en
  D_Flip_Flop #(.trigger("falling")) d_ff_15 (
    .clk(in_1), .D(ALUCalc_0a), .Q(DA_Slc_1a), .reset(in_3));  // open: Qn, preset, en
  Demultiplexer #(.enable("false")) demultiplexer_16 (
    .out0(demultiplexer_16_out0), .out1(demultiplexer_16_out1), .in(AdrSrc_1b), .sel(out_27));
  or or_18 (out_15, CS_6, out_12);
  or or_19 (out_21, CS_1, CS_2, CS_3, ALUCalc_0b, ALUCalc_0c, CS_8);
  or or_20 (out_14, R_W_1, out_28[1], DA_Slc_0a, Data_Slc_0b, CS_3, DA_Slc_1a, DA_Slc_0b, out_28[2]);
  or or_21 (out_30, out_12, ~out_15);  // OR_Gate
  or or_22 (out_13, ALUCalc_0a, ALUCalc[1]);
  or or_23 (out_19[1], AdrSrc_1a, AdrSrc_1b);
  D_Flip_Flop #(.trigger("falling")) d_ff_16 (
    .clk(in_1), .D(or_24_out), .Q(d_ff_16_q), .reset(in_3));  // open: Qn, preset, en
  or or_24 (or_24_out, Cache_En__1, ~EWC);  // OR_Gate
  or or_25 (out_28[0], Data_Slc_0a, Data_Slc_0b, DA_Slc_0b, Data_Slc_0d);
  or or_26 (out_25[0], DA_Slc_0a, DA_Slc_0b);
  or or_27 (out_25[1], DA_Slc_1a, CS_3);
  D_Flip_Flop #(.trigger("falling")) d_ff_17 (
    .clk(in_1), .D(or_28_out), .Q(PCEn_5), .reset(in_3));  // open: Qn, preset, en
  or or_28 (or_28_out, DA_Slc_1a, demultiplexer_16_out1);
  or or_29 (out_19[0], AdrSrc_0a, out_26);
  Multiplexer #(.select(2), .width(4), .enable("false")) multiplexer_1 (
    .in0(ALU_S), .in1(4'b0110), .in2(4'b0111), .out(out_31), .sel(ALUCalc));  // open: in3
  or or_30 (Cache_En__0, End_Read, End_Write);
  and and_4 (Cache_En__1, EWC, ~in_7, out_24);  // AND_Gate
  or or_31 (out_27, Cache_En__0, d_ff_16_q);
  or or_32 (out_17, Arit_End, Copia_End, PCEn_3, Arit_I_End, PCEn_5, Lw_End, PCEn_7, Especial_End);
  or or_33 (out_34, ResultLoad_1, ALUSrcB_1a, ALUCalc_0a, ALUCalc[1], ALUCalc_0b, ALUCalc_0c);
  or or_34 (out_24, CS_3, ALUCalc_0c);
  or or_35 (out_16[0], ALUCalc_0a, ALUCalc[1]);
  or or_36 (out_16[1], ALUSrcB_1a, ALUCalc_0b, ALUCalc_0c);
  or or_37 (ALUCalc[0], ALUCalc_0a, ALUCalc_0b, ALUCalc_0c);

  // Other names for the same wires on the sheet: AdrSrc[1:0] = out_19; AdrSrc_0 = out_19[0]; AdrSrc_1 = out_19[1];
  //   ALUCalc_0 = ALUCalc[0]; ALUCalc_1 = ALUCalc[1]; ALUSrcA_2 = ALUCalc[1]; ALUSrcB_0b = ALUCalc[1];
  //   ResultLoad_4 = ALUCalc[1]; ALUControl[3:0] = out_31; ALUSrcA = out_13; ALUSrcB[1:0] = out_16;
  //   ALUSrcB_0 = out_16[0]; ALUSrcB_1 = out_16[1]; BC_S[1:0] = out_22; Cache_En = out_27; CLK = in_1; CS = out_21;
  //   CS_Ram = out_15; DA_Slc[1:0] = out_25; DA_Slc_0 = out_25[0]; DA_Slc_1 = out_25[1]; Data_Slc[2:0] = out_28;
  //   Data_Slc_0 = out_28[0]; Data_Slc_1 = out_28[1]; R_W_2 = out_28[1]; Data_Slc_2 = out_28[2]; R_W_8 = out_28[2];
  //   Dirty = in_7; EQF = in_11; EXT_S = out_33; Func_Code[5:0] = in_4; Hi_Low_Load = out_18; Hit = in_5;
  //   Instr_En = out_32; is_Dirty = out_30; kbd = out_29; NF = in_10; Op_Code[5:0] = in_2; PC_En = out_17;
  //   PCEn_1 = Arit_End; PCEn_2 = Copia_End; PCEn_4 = Arit_I_End; PCEn_6 = Lw_End; PCEn_8 = Especial_End;
  //   Pila_End = PCEn_5; R_Time[3:0] = in_6; R_W_3 = DA_Slc_0a; R_W_4 = Data_Slc_0b; R_W_6 = DA_Slc_1a;
  //   Data_Slc_0c = DA_Slc_0b; R_W_7 = DA_Slc_0b; R_W_DP = out_14; CS_7 = out_12; R_W_Ram = out_12; Reset = in_3;
  //   ResultLoad = out_34; ResultLoad_2 = ALUSrcB_1a; ALUSrcA_1 = ALUCalc_0a; ALUSrcB_0a = ALUCalc_0a;
  //   ResultLoad_3 = ALUCalc_0a; ALUSrcB_1b = ALUCalc_0b; CS_4 = ALUCalc_0b; ResultLoad_5 = ALUCalc_0b; Stop = out_23;
  //   Sw_End = PCEn_7; tty = out_20; TTY_Enable = out_20; AdrSrc_0b = out_26; Value_Src = out_26; W_Time[3:0] = in_8;
  //   Write = out_24; DA_Slc_1b = CS_3; R_W_5 = CS_3; Write_1 = CS_3; ALUSrcB_1c = ALUCalc_0c; CS_5 = ALUCalc_0c;
  //   ResultLoad_6 = ALUCalc_0c; Write_2 = ALUCalc_0c; ZF = in_9

  // Notes on the sheet:
  //   Inputs
  //   Copia
  //   Instruction Operation
  //   Aritmetica
  //   Aritmetica Tipo-I
  //   Lw
  //   Sw
  //   Especial
  //   Control Unit
  //   Salto
  //   Pila
  //   Cache
  //   Outputs
  //   Enablers
  //   Selectors
endmodule

module Data_Path (
  input  Clock,
  input  Reset,
  input  Instruction_Enable,
  input  Read_Write,
  input  ALU_Result_Enable,
  input  PC_Enable,
  input  in_7,
  input  [1:0] Adress_Selector,
  input  Value_Selector,
  input  [1:0] Branch_Selector,
  input  Selector_Extend,
  input  [3:0] ALU_Selector,
  input  [31:0] RAMData,
  input  [1:0] Selector_Destination_Adress,
  input  ALU_Selector_A,
  input  [2:0] Selector_Data,
  input  [1:0] ALU_Selector_B,
  input  [6:0] KBD_ASCII_Data,
  input  KBD_available,
  output [31:0] Adress,
  output [31:0] Value,
  output [6:0] TTY_DATA,
  output ZF,
  output NF,
  output [5:0] Op_Code,
  output [5:0] Func_Code,
  output EQF
);

  wire [4:0] multiplexer_2_out, Rd, Rs, Rt;
  wire [15:0] Constante;
  wire [25:0] Destino_Salto;
  wire [31:0] ALU, alu_1_out_6, bit_extender_1_out, bit_extender_2_out, bit_extender_3_out,
       branch_control_1_out_6, Data, Hi, KBD, Lo, multiplexer_4_out, multiplexer_5_out, multiplexer_6_out,
       multiplexer_7_out, PC, Random_Generator, register_1_q, RT_t, Sp;
  wire [31:7] RS_t;

  Random #(.width(32)) u_Random_Generator (.clk(Clock), .next(Clock), .out(Random_Generator));  // open: clr
  Register #(.width(32), .trigger("falling")) register_1 (
    .D(RAMData), .en(Instruction_Enable), .Q(register_1_q), .clk(Clock), .clr(Reset));
  Register #(.width(32)) register_2 (.D(RAMData), .en(Clock), .Q(Data), .clk(Clock), .clr(Reset));
  Branch_Control branch_control_1 (
    .in_1(PC), .in_2(Constante), .in_3(Destino_Salto), .in_4({RS_t, TTY_DATA}),
    .out_6(branch_control_1_out_6), .in_5(Branch_Selector));
  assign bit_extender_1_out = {{25{1'b0}}, KBD_ASCII_Data};  // Bit_Extender bit_extender_1
  Multiplexer #(.width(32), .enable("false")) multiplexer_1 (
    .in0({32{1'b1}}), .in1(bit_extender_1_out), .out(KBD), .sel(KBD_available));
  Instruction_Decoder instruction_decoder_1 (
    .in_1(register_1_q), .out_2(Op_Code), .out_3(Destino_Salto), .out_4(Rs), .out_5(Rt), .out_6(Constante),
    .out_7(Rd), .out_8(Func_Code));
  Program_Counter program_counter_1 (
    .in_1(branch_control_1_out_6), .PC_Enable(PC_Enable), .CLK(Clock), .Reset(Reset), .out_5(PC));
  Multiplexer #(.select(2), .width(5), .enable("false")) multiplexer_2 (
    .in0(Rd), .in1(Rt), .in2({5{1'b1}}), .out(multiplexer_2_out), .sel(Selector_Destination_Adress));  // open: in3
  assign bit_extender_2_out = {{16{Constante[15]}}, Constante};  // Bit_Extender bit_extender_2
  assign bit_extender_3_out = {{16{1'b0}}, Constante};  // Bit_Extender bit_extender_3
  Multiplexer #(.select(2), .width(32), .enable("false")) multiplexer_3 (
    .in0(PC), .in1(ALU), .in2(Sp), .out(Adress), .sel(Adress_Selector));  // open: in3
  Multiplexer #(.select(3), .width(32), .enable("false")) multiplexer_4 (
    .in0(ALU), .in1(Data), .in2(Hi), .in3(Lo), .in4(Random_Generator), .in5(KBD), .out(multiplexer_4_out),
    .sel(Selector_Data));  // open: in6, in7
  Multiplexer #(.width(32), .enable("false")) multiplexer_5 (
    .in0(bit_extender_2_out), .in1(bit_extender_3_out), .out(multiplexer_5_out), .sel(Selector_Extend));
  Multiplexer #(.select(2), .width(32), .enable("false")) multiplexer_6 (
    .in0(RT_t), .in1(32'h4), .in2(multiplexer_5_out), .out(multiplexer_6_out), .sel(ALU_Selector_B));  // open: in3
  Multiplexer #(.width(32), .enable("false")) multiplexer_7 (
    .in0({RS_t, TTY_DATA}), .in1(Sp), .out(multiplexer_7_out), .sel(ALU_Selector_A));
  Multiplexer #(.width(32), .enable("false")) multiplexer_8 (
    .in0({RS_t, TTY_DATA}), .in1(RT_t), .out(Value), .sel(Value_Selector));
  ALU alu_1 (
    .in_1(Clock), .in_2(ALU_Selector), .in_3(in_7), .in_4(multiplexer_7_out), .in_5(multiplexer_6_out),
    .out_6(alu_1_out_6), .out_9(Hi), .out_11(Lo), .out_7(ZF), .out_8(NF), .out_10(EQF));
  Register_File register_file_1 (
    .Data_Input(multiplexer_4_out), .Destination_Adress(multiplexer_2_out), .in_6(Rs), .in_7(Rt),
    .Output_A({RS_t, TTY_DATA}), .Output_B(RT_t), .SP(Sp), .Read_Write(Read_Write), .Clock(Clock),
    .Reset(Reset));
  Register #(.width(32)) register_3 (.D(alu_1_out_6), .en(ALU_Result_Enable), .Q(ALU), .clk(Clock), .clr(Reset));

  // Other names for the same wires on the sheet: ALU_Slc[3:0] = ALU_Selector; ALU_Slc_A = ALU_Selector_A;
  //   ALU_Slc_B[1:0] = ALU_Selector_B; Branch_Slc[1:0] = Branch_Selector; CLK = Clock;
  //   DA_Slc[1:0] = Selector_Destination_Adress; Data_Slc[2:0] = Selector_Data; Extend_Slc = Selector_Extend;
  //   Func[5:0] = Func_Code; HL_En = in_7; Op[5:0] = Op_Code; RS_t[6:0] = TTY_DATA

  // Notes on the sheet:
  //   Inputs
  //   DATA Path
  //   Output
endmodule

module Cache (
  input  [31:0] in_1,
  input  [31:0] in_2,
  input  [31:0] in_3,
  input  [31:0] in_4,
  input  in_5,
  input  in_6,
  input  in_7,
  input  in_8,
  input  [31:0] in_9,
  input  [31:0] in_10,
  input  in_11,
  output out_12,
  output out_13,
  output [31:0] out_14,
  output [31:0] out_15,
  output [31:0] out_16,
  output [3:0] out_17,
  output [31:0] out_18,
  output [31:0] out_19,
  output [15:0] out_20
);

  wire Col_00, Col_01, Col_02, Col_03, Col_10, Col_11, Col_12, Col_13, Col_20, Col_21, Col_22, Col_23,
       Col_30, Col_31, Col_32, Col_33, Col_40, Col_41, Col_42, Col_43, Col_50, Col_51, Col_52, Col_53,
       Col_60, Col_61, Col_62, Col_63, Col_70, Col_71, Col_72, Col_73, comparator_1_eq, D0, D1, D2, D3, D4,
       D5, D6, D7, EWC, Idex_6_t, V, V0, V1, V2, V3, V4, V5, V6, V7;
  wire [3:0] En_Index0, En_Index1, En_Index2, En_Index3, En_Index4, En_Index5, En_Index6, En_Index7,
       En_Offset;
  wire [7:0] C_En_Ext, En_Index, En_Row;
  wire [26:0] T0, T1, T2, T3, T4, T5, T6, T7, Tag_star;
  wire [31:0] multiplexer_8_out, R00, R01, R02, R03, R10, R11, R12, R13, R20, R21, R22, R23, R30, R31, R32,
       R33, R40, R41, R42, R43, R50, R51, R52, R53, R60, R61, R62, R63, R70, R71, R72, R73, Value_star_star,
       Write_0, Write_1, Write_2, Write_3;

  Register #(.width(1)) R0 (.D(in_11), .en(En_Index[0]), .Q(D0), .clk(in_5), .clr(in_6));
  Register #(.width(1)) R1 (.D(in_11), .en(En_Index[1]), .Q(D1), .clk(in_5), .clr(in_6));
  Register #(.width(1)) R2 (.D(in_11), .en(En_Index[2]), .Q(D2), .clk(in_5), .clr(in_6));
  Register #(.width(1)) R3 (.D(in_11), .en(En_Index[3]), .Q(D3), .clk(in_5), .clr(in_6));
  Register #(.width(1)) R4 (.D(in_11), .en(En_Index[4]), .Q(D4), .clk(in_5), .clr(in_6));
  Register #(.width(1)) R2_2 (.D(in_11), .en(En_Index[5]), .Q(D5), .clk(in_5), .clr(in_6));
  Register #(.width(1)) R3_2 (.D(in_11), .en(Idex_6_t), .Q(D6), .clk(in_5), .clr(in_6));
  Register #(.width(1)) R4_2 (.D(in_11), .en(En_Index[7]), .Q(D7), .clk(in_5), .clr(in_6));
  Multiplexer #(.select(3), .width(32), .enable("false")) multiplexer_1 (
    .in0(R00), .in1(R10), .in2(R20), .in3(R30), .in4(R40), .in5(R50), .in6(R60), .in7(R70), .out(out_14),
    .sel(in_1[6:4]));
  Litte_Endian___Big_Endian litte_endian_big_endian_1 (.in_1(in_2), .out_2(Value_star_star));
  Register #(.width(1)) R0_2 (.D(1'b1), .en(En_Index[0]), .Q(V0), .clk(in_5), .clr(in_6));
  Register #(.width(1)) R1_2 (.D(1'b1), .en(En_Index[1]), .Q(V1), .clk(in_5), .clr(in_6));
  Register #(.width(1)) R2_3 (.D(1'b1), .en(En_Index[2]), .Q(V2), .clk(in_5), .clr(in_6));
  Register #(.width(1)) R3_3 (.D(1'b1), .en(En_Index[3]), .Q(V3), .clk(in_5), .clr(in_6));
  Register #(.width(1)) R4_3 (.D(1'b1), .en(En_Index[4]), .Q(V4), .clk(in_5), .clr(in_6));
  Register #(.width(1)) R2_4 (.D(1'b1), .en(En_Index[5]), .Q(V5), .clk(in_5), .clr(in_6));
  Register #(.width(1)) R3_4 (.D(1'b1), .en(Idex_6_t), .Q(V6), .clk(in_5), .clr(in_6));
  Register #(.width(1)) R4_4 (.D(1'b1), .en(En_Index[7]), .Q(V7), .clk(in_5), .clr(in_6));
  Multiplexer #(.select(3), .width(32), .enable("false")) multiplexer_2 (
    .in0(R01), .in1(R11), .in2(R21), .in3(R31), .in4(R41), .in5(R51), .in6(R61), .in7(R71), .out(out_15),
    .sel(in_1[6:4]));
  Multiplexer #(.width(32), .enable("false")) multiplexer_3 (
    .in0(in_3), .in1(Value_star_star), .out(Write_0), .sel(in_7));
  Register #(.width(27), .trigger("high")) R5 (
    .D({in_1[31:7], in_1[1:0]}), .en(En_Index[0]), .Q(T0), .clk(in_5), .clr(in_6));
  Register #(.width(27), .trigger("high")) R6 (
    .D({in_1[31:7], in_1[1:0]}), .en(En_Index[1]), .Q(T1), .clk(in_5), .clr(in_6));
  Register #(.width(27), .trigger("high")) R7 (
    .D({in_1[31:7], in_1[1:0]}), .en(En_Index[2]), .Q(T2), .clk(in_5), .clr(in_6));
  Register #(.width(27), .trigger("high")) R8 (
    .D({in_1[31:7], in_1[1:0]}), .en(En_Index[3]), .Q(T3), .clk(in_5), .clr(in_6));
  Register #(.width(27), .trigger("high")) R9 (
    .D({in_1[31:7], in_1[1:0]}), .en(En_Index[4]), .Q(T4), .clk(in_5), .clr(in_6));
  Register #(.width(27), .trigger("high")) R7_2 (
    .D({in_1[31:7], in_1[1:0]}), .en(En_Index[5]), .Q(T5), .clk(in_5), .clr(in_6));
  Register #(.width(27), .trigger("high")) R8_2 (
    .D({in_1[31:7], in_1[1:0]}), .en(Idex_6_t), .Q(T6), .clk(in_5), .clr(in_6));
  Register #(.width(27), .trigger("high")) R9_2 (
    .D({in_1[31:7], in_1[1:0]}), .en(En_Index[7]), .Q(T7), .clk(in_5), .clr(in_6));
  Multiplexer #(.select(3), .width(32), .enable("false")) multiplexer_4 (
    .in0(R02), .in1(R12), .in2(R22), .in3(R32), .in4(R42), .in5(R52), .in6(R62), .in7(R72), .out(out_18),
    .sel(in_1[6:4]));
  Multiplexer #(.width(32), .enable("false")) multiplexer_5 (
    .in0(in_4), .in1(Value_star_star), .out(Write_1), .sel(in_7));
  Register #(.width(32), .trigger("high")) u_R10 (.D(Write_0), .en(Col_00), .Q(R00), .clk(in_5), .clr(in_6));
  Register #(.width(32), .trigger("high")) u_R11 (.D(Write_0), .en(Col_10), .Q(R10), .clk(in_5), .clr(in_6));
  Register #(.width(32), .trigger("high")) u_R12 (.D(Write_0), .en(Col_20), .Q(R20), .clk(in_5), .clr(in_6));
  Register #(.width(32), .trigger("high")) u_R13 (.D(Write_0), .en(Col_30), .Q(R30), .clk(in_5), .clr(in_6));
  Register #(.width(32), .trigger("high")) R14 (.D(Write_0), .en(Col_40), .Q(R40), .clk(in_5), .clr(in_6));
  Register #(.width(32), .trigger("high")) R12_2 (.D(Write_0), .en(Col_50), .Q(R50), .clk(in_5), .clr(in_6));
  Register #(.width(32), .trigger("high")) R13_2 (.D(Write_0), .en(Col_60), .Q(R60), .clk(in_5), .clr(in_6));
  Register #(.width(32), .trigger("high")) R14_2 (.D(Write_0), .en(Col_70), .Q(R70), .clk(in_5), .clr(in_6));
  Multiplexer #(.select(3), .width(32), .enable("false")) multiplexer_6 (
    .in0(R03), .in1(R13), .in2(R23), .in3(R33), .in4(R43), .in5(R53), .in6(R63), .in7(R73), .out(out_19),
    .sel(in_1[6:4]));
  Comparator #(.width(27)) comparator_1 (
    .a(Tag_star), .b({in_1[31:7], in_1[1:0]}), .eq(comparator_1_eq));  // open: gt, lt
  Multiplexer #(.width(32), .enable("false")) multiplexer_7 (
    .in0(in_9), .in1(Value_star_star), .out(Write_2), .sel(in_7));
  Register #(.width(32), .trigger("high")) R15 (.D(Write_1), .en(Col_01), .Q(R01), .clk(in_5), .clr(in_6));
  Register #(.width(32), .trigger("high")) R16 (.D(Write_1), .en(Col_11), .Q(R11), .clk(in_5), .clr(in_6));
  Register #(.width(32), .trigger("high")) R17 (.D(Write_1), .en(Col_21), .Q(R21), .clk(in_5), .clr(in_6));
  Register #(.width(32), .trigger("high")) R18 (.D(Write_1), .en(Col_31), .Q(R31), .clk(in_5), .clr(in_6));
  Register #(.width(32), .trigger("high")) R19 (.D(Write_1), .en(Col_41), .Q(R41), .clk(in_5), .clr(in_6));
  Register #(.width(32), .trigger("high")) R17_2 (.D(Write_1), .en(Col_51), .Q(R51), .clk(in_5), .clr(in_6));
  Register #(.width(32), .trigger("high")) R18_2 (.D(Write_1), .en(Col_61), .Q(R61), .clk(in_5), .clr(in_6));
  Register #(.width(32), .trigger("high")) R19_2 (.D(Write_1), .en(Col_71), .Q(R71), .clk(in_5), .clr(in_6));
  and and_1 (out_13, comparator_1_eq, V);
  Multiplexer #(.select(2), .width(32), .enable("false")) multiplexer_8 (
    .in0(out_14), .in1(out_15), .in2(out_18), .in3(out_19), .out(multiplexer_8_out), .sel(in_1[3:2]));
  Register #(.width(32), .trigger("high")) u_R20 (.D(Write_2), .en(Col_02), .Q(R02), .clk(in_5), .clr(in_6));
  Register #(.width(32), .trigger("high")) u_R21 (.D(Write_2), .en(Col_12), .Q(R12), .clk(in_5), .clr(in_6));
  Register #(.width(32), .trigger("high")) u_R22 (.D(Write_2), .en(Col_22), .Q(R22), .clk(in_5), .clr(in_6));
  Register #(.width(32), .trigger("high")) u_R23 (.D(Write_2), .en(Col_32), .Q(R32), .clk(in_5), .clr(in_6));
  Register #(.width(32), .trigger("high")) R24 (.D(Write_2), .en(Col_42), .Q(R42), .clk(in_5), .clr(in_6));
  Register #(.width(32), .trigger("high")) R22_2 (.D(Write_2), .en(Col_52), .Q(R52), .clk(in_5), .clr(in_6));
  Register #(.width(32), .trigger("high")) R23_2 (.D(Write_2), .en(Col_62), .Q(R62), .clk(in_5), .clr(in_6));
  Register #(.width(32), .trigger("high")) R24_2 (.D(Write_2), .en(Col_72), .Q(R72), .clk(in_5), .clr(in_6));
  or or_1 (EWC, in_7, ~out_13);  // OR_Gate
  Litte_Endian___Big_Endian litte_endian_big_endian_2 (.in_1(multiplexer_8_out), .out_2(out_16));
  Multiplexer #(.width(32), .enable("false")) multiplexer_9 (
    .in0(in_10), .in1(Value_star_star), .out(Write_3), .sel(in_7));
  Register #(.width(32), .trigger("high")) R25 (.D(Write_3), .en(Col_03), .Q(R03), .clk(in_5), .clr(in_6));
  Register #(.width(32), .trigger("high")) R26 (.D(Write_3), .en(Col_13), .Q(R13), .clk(in_5), .clr(in_6));
  Register #(.width(32), .trigger("high")) R27 (.D(Write_3), .en(Col_23), .Q(R23), .clk(in_5), .clr(in_6));
  Register #(.width(32), .trigger("high")) R28 (.D(Write_3), .en(Col_33), .Q(R33), .clk(in_5), .clr(in_6));
  Register #(.width(32), .trigger("high")) R29 (.D(Write_3), .en(Col_43), .Q(R43), .clk(in_5), .clr(in_6));
  Register #(.width(32), .trigger("high")) R27_2 (.D(Write_3), .en(Col_53), .Q(R53), .clk(in_5), .clr(in_6));
  Register #(.width(32), .trigger("high")) R28_2 (.D(Write_3), .en(Col_63), .Q(R63), .clk(in_5), .clr(in_6));
  Register #(.width(32), .trigger("high")) R29_2 (.D(Write_3), .en(Col_73), .Q(R73), .clk(in_5), .clr(in_6));
  Decoder #(.select(2), .enable("false")) decoder_1 (
    .out0(out_17[0]), .out1(out_17[1]), .out2(out_17[2]), .out3(out_17[3]), .sel(in_1[3:2]));
  Demultiplexer #(.select(3), .enable("false")) demultiplexer_1 (
    .out0(En_Row[0]), .out1(En_Row[1]), .out2(En_Row[2]), .out3(En_Row[3]), .out4(En_Row[4]),
    .out5(En_Row[5]), .out6(En_Row[6]), .out7(En_Row[7]), .in(EWC), .sel(in_1[6:4]));
  Multiplexer #(.width(4), .enable("false")) multiplexer_10 (.in0(4'b1111), .in1(out_17), .out(En_Offset), .sel(in_7));
  Multiplexer #(.select(3), .width(27), .enable("false")) multiplexer_11 (
    .in0(T0), .in1(T1), .in2(T2), .in3(T3), .in4(T4), .in5(T5), .in6(T6), .in7(T7), .out(Tag_star),
    .sel(in_1[6:4]));
  Multiplexer #(.select(3), .enable("false")) multiplexer_12 (
    .in0(V0), .in1(V1), .in2(V2), .in3(V3), .in4(V4), .in5(V5), .in6(V6), .in7(V7), .out(V), .sel(in_1[6:4]));
  Multiplexer #(.select(3), .enable("false")) multiplexer_13 (
    .in0(D0), .in1(D1), .in2(D2), .in3(D3), .in4(D4), .in5(D5), .in6(D6), .in7(D7), .out(out_12),
    .sel(in_1[6:4]));
  assign En_Index0 = {{3{En_Index[0]}}, En_Index[0]};  // Bit_Extender bit_extender_1
  assign En_Index1 = {{3{En_Index[1]}}, En_Index[1]};  // Bit_Extender bit_extender_2
  assign En_Index2 = {{3{En_Index[2]}}, En_Index[2]};  // Bit_Extender bit_extender_3
  assign En_Index3 = {{3{En_Index[3]}}, En_Index[3]};  // Bit_Extender bit_extender_4
  assign C_En_Ext = {{7{in_8}}, in_8};  // Bit_Extender bit_extender_5
  assign {Col_03, Col_02, Col_01, Col_00} = En_Offset & En_Index0;  // AND_Gate and_2, 4 bits wide
  assign {Col_13, Col_12, Col_11, Col_10} = En_Offset & En_Index1;  // AND_Gate and_3, 4 bits wide
  assign {Col_23, Col_22, Col_21, Col_20} = En_Offset & En_Index2;  // AND_Gate and_4, 4 bits wide
  assign {Col_33, Col_32, Col_31, Col_30} = En_Offset & En_Index3;  // AND_Gate and_5, 4 bits wide
  assign En_Index4 = {{3{En_Index[4]}}, En_Index[4]};  // Bit_Extender bit_extender_6
  assign En_Index5 = {{3{En_Index[5]}}, En_Index[5]};  // Bit_Extender bit_extender_7
  assign En_Index6 = {{3{Idex_6_t}}, Idex_6_t};  // Bit_Extender bit_extender_8
  assign En_Index7 = {{3{En_Index[7]}}, En_Index[7]};  // Bit_Extender bit_extender_9
  assign En_Index = En_Row & C_En_Ext;  // AND_Gate and_6, 8 bits wide
  assign {Col_43, Col_42, Col_41, Col_40} = En_Offset & En_Index4;  // AND_Gate and_7, 4 bits wide
  assign {Col_53, Col_52, Col_51, Col_50} = En_Offset & En_Index5;  // AND_Gate and_8, 4 bits wide
  assign {Col_63, Col_62, Col_61, Col_60} = En_Offset & En_Index6;  // AND_Gate and_9, 4 bits wide
  assign {Col_73, Col_72, Col_71, Col_70} = En_Offset & En_Index7;  // AND_Gate and_10, 4 bits wide

  assign out_20 = in_1[19:4];

  // Other names for the same wires on the sheet: Block0[31:0] = in_3; Block1[31:0] = in_4; Block2[31:0] = in_9;
  //   Block3[31:0] = in_10; Cache_En = in_8; Clock = in_5; Data[31:0] = out_16; Dirty = out_12; Idex_0 = En_Index[0];
  //   Idex_1 = En_Index[1]; Idex_2 = En_Index[2]; Idex_3 = En_Index[3]; Idex_4 = En_Index[4]; Idex_5 = En_Index[5];
  //   Idex_6 = En_Index[6]; Idex_7 = En_Index[7]; HIT = out_13; Tag[26:0] = {in_1[31:7], in_1[1:0]};
  //   Offset[1:0] = in_1[3:2]; Address[15:0] = in_1[19:4]; Index[2:0] = in_1[6:4]; is_Dirty = in_11;
  //   Mask[3:0] = out_17; Out0[31:0] = out_14; Out1[31:0] = out_15; Out2[31:0] = out_18; Out3[31:0] = out_19;
  //   ReadWrite = in_7; Reset = in_6; Value[31:0] = in_2

  // Notes on the sheet:
  //   in_7: pull=down
  //   Instruction
  //   Dirty
  //   Inputs
  //   Validate
  //   Cache
  //   Tag
  //   Block 0
  //   Block 2
  //   Block 1
  //   Block 3
  //   Outputs
  //   Offset
  //   Block 0
  //   Block 2
  //   Block 1
  //   Block 3
endmodule

module Instruction_Decoder (
  input  [31:0] in_1,
  output [5:0] out_2,
  output [25:0] out_3,
  output [4:0] out_4,
  output [4:0] out_5,
  output [15:0] out_6,
  output [4:0] out_7,
  output [5:0] out_8
);


  assign out_2 = in_1[31:26];
  assign out_3 = in_1[25:0];
  assign out_4 = in_1[25:21];
  assign out_5 = in_1[20:16];
  assign out_6 = in_1[15:0];
  assign out_7 = in_1[15:11];
  assign out_8 = in_1[5:0];

  // Other names for the same wires on the sheet: Constante[15:0] = in_1[15:0]; Destino_Salto[25:0] = in_1[25:0];
  //   Func_Code[5:0] = in_1[5:0]; Rd[4:0] = in_1[15:11]; Rt[4:0] = in_1[20:16]; Rs[4:0] = in_1[25:21];
  //   Op_Code[5:0] = in_1[31:26]

  // Notes on the sheet:
  //   Instruction Decoder
  //   Outputs
endmodule

module Program_Counter (
  input  [31:0] in_1,
  input  PC_Enable,
  input  CLK,
  input  Reset,
  output [31:0] out_5
);

  Register #(.width(32)) register_1 (.D(in_1), .en(PC_Enable), .Q(out_5), .clk(CLK), .clr(Reset));

  // Notes on the sheet:
  //   PC' (next instruction)
  //   Program Counter
  //   PC (current instruction)
endmodule

module Litte_Endian___Big_Endian (
  input  [31:0] in_1,
  output [31:0] out_2
);


  assign out_2 = {in_1[7:0], in_1[15:8], in_1[23:16], in_1[31:24]};

  // Notes on the sheet:
  //   Input
  //   Litle - Big Endian
  //   Output
endmodule

module ALU (
  input  in_1,
  input  [3:0] in_2,
  input  in_3,
  input  [31:0] in_4,
  input  [31:0] in_5,
  output [31:0] out_6,
  output out_7,
  output out_8,
  output [31:0] out_9,
  output out_10,
  output [31:0] out_11
);

  wire comparator_1_lt;
  wire [1:0] Selector_Mult_Div;
  wire [31:0] ADD, AND, divider_1_out, divider_1_rem, multiplexer_1_out, multiplexer_2_out,
       multiplier_1_cout, NOR, OR, signed_divider_1_carry_out, signed_divider_1_result,
       signed_multiplier_1_out_3, signed_multiplier_1_out_4, SLT, SUB, XOR;

  assign AND = in_4 & in_5;  // AND_Gate and_1, 32 bits wide
  assign OR = in_4 | in_5;  // OR_Gate or_1, 32 bits wide
  assign NOR = ~(in_4 | in_5);  // NOR_Gate nor_1, 32 bits wide
  assign XOR = in_4 ^ in_5;  // XOR_Gate xor_1, 32 bits wide
  Signed_Multiplier signed_multiplier_1 (
    .in_1(in_4), .in_2(in_5), .out_3(signed_multiplier_1_out_3), .out_4(signed_multiplier_1_out_4));
  Multiplier #(.width(32)) multiplier_1 (
    .a(in_4), .b(in_5), .out(signed_multiplier_1_out_3), .cout(multiplier_1_cout));  // open: cin
  Signed_Divider signed_divider_1 (
    .in_1(in_4), .in_2(in_5), .Result(signed_divider_1_result), .Carry_Out(signed_divider_1_carry_out));
  Divider #(.width(32)) divider_1 (.a(in_4), .b(in_5), .out(divider_1_out), .rem(divider_1_rem));  // open: upper
  Adder #(.width(32)) adder_1 (.a(in_4), .b(in_5), .out(ADD));  // open: cin, cout
  Subtractor #(.width(32)) subtractor_1 (.a(in_4), .b(in_5), .out(SUB));  // open: bin, bout
  Comparator #(.width(32)) comparator_1 (.a(in_4), .b(in_5), .eq(out_10), .lt(comparator_1_lt));  // open: gt
  assign SLT = {{31{1'b0}}, comparator_1_lt};  // Bit_Extender bit_extender_1
  Multiplexer #(.select(2), .width(32), .enable("false")) multiplexer_1 (
    .in0(signed_multiplier_1_out_4), .in1(multiplier_1_cout), .in2(signed_divider_1_carry_out),
    .in3(divider_1_rem), .out(multiplexer_1_out), .sel(Selector_Mult_Div));
  Multiplexer #(.select(2), .width(32), .enable("false")) multiplexer_2 (
    .in0(signed_multiplier_1_out_3), .in1(signed_multiplier_1_out_3), .in2(signed_divider_1_result),
    .in3(divider_1_out), .out(multiplexer_2_out), .sel(Selector_Mult_Div));
  Register #(.width(32)) register_1 (.D(multiplexer_1_out), .en(in_3), .Q(out_9), .clk(in_1));  // open: clr
  Register #(.width(32)) register_2 (.D(multiplexer_2_out), .en(in_3), .Q(out_11), .clk(in_1));  // open: clr
  Multiplexer #(.select(4), .width(32), .enable("false")) multiplexer_3 (
    .in0(AND), .in1(OR), .in2(NOR), .in3(XOR), .in4(SLT), .in5(SLT), .in6(ADD), .in7(SUB), .out(out_6),
    .sel(in_2));  // open: in8, in9, in10, in11, in12, in13, in14, in15
  and and_2 (Selector_Mult_Div[0], in_2[3], ~in_2[2], in_2[0]);  // AND_Gate
  and and_3 (Selector_Mult_Div[1], in_2[1], ~in_2[2], in_2[3]);  // AND_Gate
  Comparator #(.width(32)) comparator_2 (.a(in_4), .b({32{1'b0}}), .eq(out_7), .lt(out_8));  // open: gt

  // Other names for the same wires on the sheet: A[31:0] = in_4; ALU_Selector[3:0] = in_2; B[31:0] = in_5; CLK = in_1;
  //   Enable_H_L = in_3; EQF = out_10; HIGH[31:0] = out_9; LOW[31:0] = out_11; NF = out_8; Output[31:0] = out_6;
  //   SLTU[31:0] = SLT; ZF = out_7

  // Notes on the sheet:
  //   Inputs
  //   Mult
  //   Div
  //   ALU
  //    (Restos)
  //   (Resultados)
  //   Outputs
endmodule

module Signed_Divider (
  input  [31:0] in_1,
  input  [31:0] in_2,
  output [31:0] Result,
  output [31:0] Carry_Out
);

  wire xor_1_out;
  wire [31:0] divider_1_out, multiplexer_1_out, multiplexer_2_out, negator_1_out, negator_2_out,
       negator_3_out;

  // Probe on in_1
  // Probe on in_2
  Negator #(.width(32)) negator_1 (.in(in_1), .out(negator_1_out));
  Negator #(.width(32)) negator_2 (.in(in_2), .out(negator_2_out));
  Multiplexer #(.width(32), .enable("false")) multiplexer_1 (
    .in0(in_1), .in1(negator_1_out), .out(multiplexer_1_out), .sel(in_1[31]));
  Multiplexer #(.width(32), .enable("false")) multiplexer_2 (
    .in0(in_2), .in1(negator_2_out), .out(multiplexer_2_out), .sel(in_2[31]));
  Divider #(.width(32)) divider_1 (
    .a(multiplexer_1_out), .b(multiplexer_2_out), .out(divider_1_out), .rem(Carry_Out));  // open: upper
  xor xor_1 (xor_1_out, in_1[31], in_2[31]);
  Negator #(.width(32)) negator_3 (.in(divider_1_out), .out(negator_3_out));
  // Probe on Carry_Out
  Multiplexer #(.width(32), .enable("false")) multiplexer_3 (
    .in0(divider_1_out), .in1(negator_3_out), .out(Result), .sel(xor_1_out));
  // Probe on Result

  // Notes on the sheet:
  //   A
  //   B
  //   Signed Divider
endmodule

module Signed_Multiplier (
  input  [31:0] in_1,
  input  [31:0] in_2,
  output [31:0] out_3,
  output [31:0] out_4
);

  wire adder_1_cout, xor_1_out;
  wire [31:0] adder_1_out, adder_2_out, multiplexer_1_out, multiplexer_2_out, multiplier_1_cout,
       multiplier_1_out, negator_1_out, negator_2_out, not_1_out, not_2_out;

  // Probe on in_1
  // Probe on in_2
  Negator #(.width(32)) negator_1 (.in(in_1), .out(negator_1_out));
  Negator #(.width(32)) negator_2 (.in(in_2), .out(negator_2_out));
  Multiplexer #(.width(32), .enable("false")) multiplexer_1 (
    .in0(in_1), .in1(negator_1_out), .out(multiplexer_1_out), .sel(in_1[31]));
  Multiplexer #(.width(32), .enable("false")) multiplexer_2 (
    .in0(in_2), .in1(negator_2_out), .out(multiplexer_2_out), .sel(in_2[31]));
  Multiplier #(.width(32)) multiplier_1 (
    .a(multiplexer_1_out), .b(multiplexer_2_out), .out(multiplier_1_out), .cout(multiplier_1_cout));  // open: cin
  xor xor_1 (xor_1_out, in_1[31], in_2[31]);
  // Probe on multiplier_1_out
  assign not_1_out = ~multiplier_1_out;  // NOT_Gate not_1, 32 bits wide
  assign not_2_out = ~multiplier_1_cout;  // NOT_Gate not_2, 32 bits wide
  Adder #(.width(32)) adder_1 (.a(not_1_out), .b(32'h1), .out(adder_1_out), .cout(adder_1_cout));  // open: cin
  Adder #(.width(32)) adder_2 (.a(not_2_out), .b({32{1'b0}}), .out(adder_2_out), .cin(adder_1_cout));  // open: cout
  Multiplexer #(.width(32), .enable("false")) multiplexer_3 (
    .in0(multiplier_1_out), .in1(adder_1_out), .out(out_3), .sel(xor_1_out));
  Multiplexer #(.width(32), .enable("false")) multiplexer_4 (
    .in0(multiplier_1_cout), .in1(adder_2_out), .out(out_4), .sel(xor_1_out));
  // Probe on out_3
  // Probe on out_4

  // Notes on the sheet:
  //   A
  //   B
  //   Signed Multiplier
endmodule

module Branch_Control (
  input  [31:0] in_1,
  input  [15:0] in_2,
  input  [25:0] in_3,
  input  [31:0] in_4,
  input  [1:0] in_5,
  output [31:0] out_6
);

  wire [15:0] multiplier_1_out;
  wire [31:0] bit_extender_1_out, PC__4, PC__4_Offset_4, Rs_t;

  Adder #(.width(32)) adder_1 (.a(in_1), .b(32'h4), .out(PC__4));  // open: cin, cout
  assign bit_extender_1_out = {{16{multiplier_1_out[15]}}, multiplier_1_out};  // Bit_Extender bit_extender_1
  Multiplier #(.width(16)) multiplier_1 (.a(in_2), .b(16'h4), .out(multiplier_1_out));  // open: cin, cout
  Adder #(.width(32)) adder_2 (.a(PC__4), .b(bit_extender_1_out), .out(PC__4_Offset_4));  // open: cin, cout
  Multiplexer #(.select(2), .width(32), .enable("false")) multiplexer_1 (
    .in0(PC__4), .in1(PC__4_Offset_4), .in2({in_1[31:28], in_3, 2'b00}), .in3(Rs_t), .out(out_6), .sel(in_5));

  // Other names for the same wires on the sheet: BS[1:0] = in_5; Destino[25:0] = in_3;
  //   Jump[31:2] = {in_1[31:28], in_3}; Offset[15:0] = in_2; PC[31:0] = in_1; PC_star[31:0] = out_6; RS[31:0] = in_4

  // Notes on the sheet:
  //   Inputs
  //   Branch Control
  //   Output
endmodule

module Register_File (
  input  Read_Write,
  input  Clock,
  input  Reset,
  input  [31:0] Data_Input,
  input  [4:0] Destination_Adress,
  input  [4:0] in_6,
  input  [4:0] in_7,
  output [31:0] Output_A,
  output [31:0] Output_B,
  output [31:0] SP
);

  wire Input_0, Input_1, Input_2, Input_3, Input_4, Input_5, Input_6, Input_7, Input_8, Input_9, Input_10,
       Input_11, Input_12, Input_13, Input_14, Input_15, Input_16, Input_17, Input_18, Input_19, Input_20,
       Input_21, Input_22, Input_23, Input_24, Input_25, Input_26, Input_27, Input_28, Input_29, Input_30,
       Input_31;
  wire [31:0] R0, R1, R2, R3, R4, R5, R6, R7, R8, R9, R10, R11, R12, R13, R14, R15, R16, R17, R18, R19, R20,
       R21, R22, R23, R24, R25, R26, R27, R28, R29, R30;

  Demultiplexer #(.select(5), .enable("false")) demultiplexer_1 (
    .out0(Input_0), .out1(Input_1), .out2(Input_2), .out3(Input_3), .out4(Input_4), .out5(Input_5),
    .out6(Input_6), .out7(Input_7), .out8(Input_8), .out9(Input_9), .out10(Input_10), .out11(Input_11),
    .out12(Input_12), .out13(Input_13), .out14(Input_14), .out15(Input_15), .out16(Input_16),
    .out17(Input_17), .out18(Input_18), .out19(Input_19), .out20(Input_20), .out21(Input_21),
    .out22(Input_22), .out23(Input_23), .out24(Input_24), .out25(Input_25), .out26(Input_26),
    .out27(Input_27), .out28(Input_28), .out29(Input_29), .out30(Input_30), .out31(Input_31),
    .in(Read_Write), .sel(Destination_Adress));
  Register #(.width(32)) u_R0 (.D({32{1'b0}}), .en(Input_0), .Q(R0), .clk(Clock), .clr(Reset));
  Register #(.width(32)) u_R1 (.D(Data_Input), .en(Input_1), .Q(R1), .clk(Clock), .clr(Reset));
  Register #(.width(32)) u_R2 (.D(Data_Input), .en(Input_2), .Q(R2), .clk(Clock), .clr(Reset));
  Register #(.width(32)) u_R3 (.D(Data_Input), .en(Input_3), .Q(R3), .clk(Clock), .clr(Reset));
  Register #(.width(32)) u_R4 (.D(Data_Input), .en(Input_4), .Q(R4), .clk(Clock), .clr(Reset));
  Register #(.width(32)) u_R5 (.D(Data_Input), .en(Input_5), .Q(R5), .clk(Clock), .clr(Reset));
  Register #(.width(32)) u_R6 (.D(Data_Input), .en(Input_6), .Q(R6), .clk(Clock), .clr(Reset));
  Register #(.width(32)) u_R7 (.D(Data_Input), .en(Input_7), .Q(R7), .clk(Clock), .clr(Reset));
  Register #(.width(32)) u_R8 (.D(Data_Input), .en(Input_8), .Q(R8), .clk(Clock), .clr(Reset));
  Register #(.width(32)) u_R9 (.D(Data_Input), .en(Input_9), .Q(R9), .clk(Clock), .clr(Reset));
  Register #(.width(32)) u_R10 (.D(Data_Input), .en(Input_10), .Q(R10), .clk(Clock), .clr(Reset));
  Register #(.width(32)) u_R11 (.D(Data_Input), .en(Input_11), .Q(R11), .clk(Clock), .clr(Reset));
  Register #(.width(32)) u_R12 (.D(Data_Input), .en(Input_12), .Q(R12), .clk(Clock), .clr(Reset));
  Register #(.width(32)) u_R13 (.D(Data_Input), .en(Input_13), .Q(R13), .clk(Clock), .clr(Reset));
  Register #(.width(32)) u_R14 (.D(Data_Input), .en(Input_14), .Q(R14), .clk(Clock), .clr(Reset));
  Register #(.width(32)) u_R15 (.D(Data_Input), .en(Input_15), .Q(R15), .clk(Clock), .clr(Reset));
  Register #(.width(32)) u_R16 (.D(Data_Input), .en(Input_16), .Q(R16), .clk(Clock), .clr(Reset));
  Register #(.width(32)) u_R17 (.D(Data_Input), .en(Input_17), .Q(R17), .clk(Clock), .clr(Reset));
  Register #(.width(32)) u_R18 (.D(Data_Input), .en(Input_18), .Q(R18), .clk(Clock), .clr(Reset));
  Register #(.width(32)) u_R19 (.D(Data_Input), .en(Input_19), .Q(R19), .clk(Clock), .clr(Reset));
  Register #(.width(32)) u_R20 (.D(Data_Input), .en(Input_20), .Q(R20), .clk(Clock), .clr(Reset));
  Register #(.width(32)) u_R21 (.D(Data_Input), .en(Input_21), .Q(R21), .clk(Clock), .clr(Reset));
  Register #(.width(32)) u_R22 (.D(Data_Input), .en(Input_22), .Q(R22), .clk(Clock), .clr(Reset));
  Register #(.width(32)) u_R23 (.D(Data_Input), .en(Input_23), .Q(R23), .clk(Clock), .clr(Reset));
  Register #(.width(32)) u_R24 (.D(Data_Input), .en(Input_24), .Q(R24), .clk(Clock), .clr(Reset));
  Multiplexer #(.select(5), .width(32), .enable("false")) multiplexer_1 (
    .in0(R0), .in1(R1), .in2(R2), .in3(R3), .in4(R4), .in5(R5), .in6(R6), .in7(R7), .in8(R8), .in9(R9),
    .in10(R10), .in11(R11), .in12(R12), .in13(R13), .in14(R14), .in15(R15), .in16(R16), .in17(R17),
    .in18(R18), .in19(R19), .in20(R20), .in21(R21), .in22(R22), .in23(R23), .in24(R24), .in25(R25),
    .in26(R26), .in27(R27), .in28(R28), .in29(R29), .in30(R30), .in31(SP), .out(Output_A), .sel(in_6));
  Register #(.width(32)) u_R25 (.D(Data_Input), .en(Input_25), .Q(R25), .clk(Clock), .clr(Reset));
  Register #(.width(32)) u_R26 (.D(Data_Input), .en(Input_26), .Q(R26), .clk(Clock), .clr(Reset));
  Register #(.width(32)) u_R27 (.D(Data_Input), .en(Input_27), .Q(R27), .clk(Clock), .clr(Reset));
  Register #(.width(32)) u_R28 (.D(Data_Input), .en(Input_28), .Q(R28), .clk(Clock), .clr(Reset));
  Register #(.width(32)) u_R29 (.D(Data_Input), .en(Input_29), .Q(R29), .clk(Clock), .clr(Reset));
  Register #(.width(32)) u_R30 (.D(Data_Input), .en(Input_30), .Q(R30), .clk(Clock), .clr(Reset));
  Register #(.width(32)) u_SP (.D(Data_Input), .en(Input_31), .Q(SP), .clk(Clock), .clr(Reset));
  Multiplexer #(.select(5), .width(32), .enable("false")) multiplexer_2 (
    .in0(R0), .in1(R1), .in2(R2), .in3(R3), .in4(R4), .in5(R5), .in6(R6), .in7(R7), .in8(R8), .in9(R9),
    .in10(R10), .in11(R11), .in12(R12), .in13(R13), .in14(R14), .in15(R15), .in16(R16), .in17(R17),
    .in18(R18), .in19(R19), .in20(R20), .in21(R21), .in22(R22), .in23(R23), .in24(R24), .in25(R25),
    .in26(R26), .in27(R27), .in28(R28), .in29(R29), .in30(R30), .in31(SP), .out(Output_B), .sel(in_7));

  // Other names for the same wires on the sheet: Data[31:0] = Data_Input; Destination[4:0] = Destination_Adress;
  //   R31[31:0] = SP; ReadWrite = Read_Write; Selector_A[4:0] = in_6; Selector_B[4:0] = in_7

  // Notes on the sheet:
  //   Inputs
  //   Register File
  //   Outputs
endmodule

module Operation_Decoder (
  input  [5:0] Inputs,
  input  [5:0] in_2,
  input  in_3,
  input  in_4,
  input  in_5,
  output [3:0] out_6,
  output [2:0] out_7,
  output [1:0] out_8,
  output out_9
);

  wire _00_0000, _11_1000, _11_1111, add, addi, \and , and_23_out, and_24_out, and_25_out, and_26_out,
       and_27_out, and_28_out, and_29_out, andi, Arit_I, Aritmetica, beq, bgtz, blez, bltz, bne,
       comparator_1_eq, comparator_2_eq, comparator_3_eq, comparator_4_eq, comparator_5_eq, comparator_6_eq,
       comparator_8_eq, comparator_9_eq, comparator_10_eq, comparator_11_eq, comparator_18_eq,
       comparator_19_eq, comparator_22_eq, comparator_23_eq, comparator_24_eq, comparator_25_eq,
       comparator_32_eq, comparator_33_eq, comparator_34_eq, comparator_35_eq, comparator_36_eq,
       comparator_37_eq, comparator_40_lt, comparator_41_eq, comparator_41_gt, comparator_42_lt,
       comparator_43_gt, comparator_44_lt, comparator_45_gt, Copia, div, divu, halt, j, jr, kbd, lw, mfhi,
       mflo, mult, mulu, nop, \nor , \or , or_3_out, ori, pop, push, rnd, Rs__0_t, Rs___0, Rs____Rt, Salto,
       slt, slti, sltiu, sltu, sub, sw, tty, \xor , xori;
  wire [1:0] BC_S;

  Comparator #(.width(6)) comparator_1 (.a(in_2), .b(6'b100000), .eq(comparator_1_eq));  // open: gt, lt
  Comparator #(.width(6)) comparator_2 (.a(in_2), .b(6'b100010), .eq(comparator_2_eq));  // open: gt, lt
  Comparator #(.width(6)) comparator_3 (.a(in_2), .b(6'b011000), .eq(comparator_3_eq));  // open: gt, lt
  Comparator #(.width(6)) comparator_4 (.a(in_2), .b(6'b011001), .eq(comparator_4_eq));  // open: gt, lt
  Comparator #(.width(6)) comparator_5 (.a(in_2), .b(6'b011010), .eq(comparator_5_eq));  // open: gt, lt
  Comparator #(.width(6)) comparator_6 (.a(in_2), .b(6'b011011), .eq(comparator_6_eq));  // open: gt, lt
  Comparator #(.width(6)) comparator_7 (.a(Inputs), .b(6'b001000), .eq(addi));  // open: gt, lt
  and and_1 (add, _00_0000, comparator_1_eq);
  and and_2 (sub, _00_0000, comparator_2_eq);
  and and_3 (mult, _00_0000, comparator_3_eq);
  and and_4 (mulu, _00_0000, comparator_4_eq);
  and and_5 (div, _00_0000, comparator_5_eq);
  and and_6 (divu, _00_0000, comparator_6_eq);
  Comparator #(.width(6)) comparator_8 (.a(in_2), .b(6'b100100), .eq(comparator_8_eq));  // open: gt, lt
  Comparator #(.width(6)) comparator_9 (.a(in_2), .b(6'b100101), .eq(comparator_9_eq));  // open: gt, lt
  Comparator #(.width(6)) comparator_10 (.a(in_2), .b(6'b100111), .eq(comparator_10_eq));  // open: gt, lt
  Comparator #(.width(6)) comparator_11 (.a(in_2), .b(6'b101000), .eq(comparator_11_eq));  // open: gt, lt
  Comparator #(.width(6)) comparator_12 (.a(Inputs), .b(6'b001100), .eq(andi));  // open: gt, lt
  Comparator #(.width(6)) comparator_13 (.a(Inputs), .b(6'b001101), .eq(ori));  // open: gt, lt
  Comparator #(.width(6)) comparator_14 (.a(Inputs), .b(6'b001110), .eq(xori));  // open: gt, lt
  Comparator #(.width(6)) comparator_15 (.a(Inputs), .b({6{1'b0}}), .eq(_00_0000));  // open: gt, lt
  Comparator #(.width(6)) comparator_16 (.a(Inputs), .b({6{1'b1}}), .eq(_11_1111));  // open: gt, lt
  and and_7 (\and , _00_0000, comparator_8_eq);
  and and_8 (\or , _00_0000, comparator_9_eq);
  and and_9 (\nor , _00_0000, comparator_10_eq);
  and and_10 (\xor , _00_0000, comparator_11_eq);
  Comparator #(.width(6)) comparator_17 (.a(Inputs), .b(6'b111000), .eq(_11_1000));  // open: gt, lt
  Comparator #(.width(6)) comparator_18 (.a(in_2), .b(6'b101010), .eq(comparator_18_eq));  // open: gt, lt
  Comparator #(.width(6)) comparator_19 (.a(in_2), .b(6'b101011), .eq(comparator_19_eq));  // open: gt, lt
  Comparator #(.width(6)) comparator_20 (.a(Inputs), .b(6'b001010), .eq(slti));  // open: gt, lt
  Comparator #(.width(6)) comparator_21 (.a(Inputs), .b(6'b001011), .eq(sltiu));  // open: gt, lt
  and and_11 (slt, _00_0000, comparator_18_eq);
  and and_12 (sltu, _00_0000, comparator_19_eq);
  or or_1 (out_9, andi, ori, xori);
  Comparator #(.width(6)) comparator_22 (.a(in_2), .b(6'b010000), .eq(comparator_22_eq));  // open: gt, lt
  Comparator #(.width(6)) comparator_23 (.a(in_2), .b(6'b010010), .eq(comparator_23_eq));  // open: gt, lt
  and and_13 (mfhi, _00_0000, comparator_22_eq);
  and and_14 (mflo, _00_0000, comparator_23_eq);
  Comparator #(.width(6)) comparator_24 (.a(in_2), .b({6{1'b0}}), .eq(comparator_24_eq));  // open: gt, lt
  Comparator #(.width(6)) comparator_25 (.a(in_2), .b(6'b001000), .eq(comparator_25_eq));  // open: gt, lt
  and and_15 (nop, _00_0000, comparator_24_eq);
  and and_16 (jr, _00_0000, comparator_25_eq);
  Comparator #(.width(6)) comparator_26 (.a(Inputs), .b(6'b000100), .eq(beq));  // open: gt, lt
  Comparator #(.width(6)) comparator_27 (.a(Inputs), .b(6'b000101), .eq(bne));  // open: gt, lt
  Comparator #(.width(6)) comparator_28 (.a(Inputs), .b(6'b000110), .eq(blez));  // open: gt, lt
  Comparator #(.width(6)) comparator_29 (.a(Inputs), .b(6'b000111), .eq(bgtz));  // open: gt, lt
  Comparator #(.width(6)) comparator_30 (.a(Inputs), .b(6'b000001), .eq(bltz));  // open: gt, lt
  Comparator #(.width(6)) comparator_31 (.a(Inputs), .b(6'b000010), .eq(j));  // open: gt, lt
  ALU_Encoder alu_encoder_1 (
    .ADD(add), .ADDI(addi), .SUB(sub), .Type_I(Arit_I), .MULT(mult), .MULU(mulu), .DIV(div), .DIVU(divu),
    .AND(\and ), .ANDI(andi), .OR(\or ), .ORI(ori), .XOR(\xor ), .XORI(xori), .ALU_SELECTOR(out_6),
    .NOR(\nor ), .SLT(slt), .SLTI(slti), .SLTU(sltu), .SLTIU(sltiu));
  Comparator #(.width(6)) comparator_32 (.a(in_2), .b({6{1'b1}}), .eq(comparator_32_eq));  // open: gt, lt
  Comparator #(.width(6)) comparator_33 (.a(in_2), .b(6'b000001), .eq(comparator_33_eq));  // open: gt, lt
  Comparator #(.width(6)) comparator_34 (.a(in_2), .b(6'b000010), .eq(comparator_34_eq));  // open: gt, lt
  Comparator #(.width(6)) comparator_35 (.a(in_2), .b(6'b000100), .eq(comparator_35_eq));  // open: gt, lt
  and and_17 (halt, _11_1111, comparator_32_eq);
  and and_18 (tty, _11_1111, comparator_33_eq);
  and and_19 (rnd, _11_1111, comparator_34_eq);
  and and_20 (kbd, _11_1111, comparator_35_eq);
  or or_2 (Rs___0, in_3, in_4);
  not not_1 (Rs__0_t, Rs___0);
  not not_2 (Rs____Rt, in_5);
  Comparator #(.width(6)) comparator_36 (.a(in_2), .b({6{1'b0}}), .eq(comparator_36_eq));  // open: gt, lt
  Comparator #(.width(6)) comparator_37 (.a(in_2), .b(6'b000001), .eq(comparator_37_eq));  // open: gt, lt
  Comparator #(.width(6)) comparator_38 (.a(Inputs), .b(6'b100011), .eq(lw));  // open: gt, lt
  Comparator #(.width(6)) comparator_39 (.a(Inputs), .b(6'b101011), .eq(sw));  // open: gt, lt
  and and_21 (pop, _11_1000, comparator_36_eq);
  and and_22 (push, _11_1000, comparator_37_eq);
  and and_23 (and_23_out, beq, in_5);
  and and_24 (and_24_out, bne, Rs____Rt);
  and and_25 (and_25_out, blez, Rs___0);
  and and_26 (and_26_out, bgtz, Rs__0_t);
  and and_27 (and_27_out, bltz, in_4);
  or or_3 (or_3_out, and_23_out, and_24_out, and_25_out, and_26_out, and_27_out);
  or or_4 (BC_S[0], or_3_out, jr);
  or or_5 (BC_S[1], jr, j);
  Comparator #(.width(6), .mode("unsigned")) comparator_40 (
    .a(Inputs), .b(6'b001000), .lt(comparator_40_lt));  // open: gt, eq
  Comparator #(.width(6), .mode("unsigned")) comparator_41 (
    .a(Inputs), .b({6{1'b0}}), .gt(comparator_41_gt), .eq(comparator_41_eq));  // open: lt
  Comparator #(.width(6), .mode("unsigned")) comparator_42 (
    .a(in_2), .b(6'b001001), .lt(comparator_42_lt));  // open: gt, eq
  Comparator #(.width(6), .mode("unsigned")) comparator_43 (
    .a(in_2), .b(6'b001111), .gt(comparator_43_gt));  // open: eq, lt
  Comparator #(.width(6), .mode("unsigned")) comparator_44 (
    .a(in_2), .b(6'b010011), .lt(comparator_44_lt));  // open: gt, eq
  Comparator #(.width(6), .mode("unsigned")) comparator_45 (
    .a(in_2), .b(6'b010111), .gt(comparator_45_gt));  // open: eq, lt
  and and_28 (and_28_out, comparator_40_lt, comparator_41_gt);
  and and_29 (and_29_out, comparator_41_eq, comparator_42_lt);
  or or_6 (Salto, and_28_out, and_29_out);
  and and_30 (Copia, comparator_41_eq, comparator_43_gt, comparator_44_lt);
  and and_31 (Aritmetica, comparator_41_eq, comparator_45_gt);
  or or_7 (out_7[0], Copia, Arit_I, lw, _11_1111);
  or or_8 (out_7[1], Salto, Arit_I, sw, _11_1111);
  or or_9 (out_7[2], _11_1000, lw, sw, _11_1111);

  // Other names for the same wires on the sheet: ALU_S[3:0] = out_6; BC_S_t[1:0] = out_8; Demul_S[2:0] = out_7;
  //   EXT_S = out_9; Func_Code[5:0] = in_2; Op_Code[5:0] = Inputs; NF = in_4; Rs__0 = in_4; EQF = in_5;
  //   Rs____Rt_t = in_5; ZF = in_3

  // Notes on the sheet:
  //   Aritmeticas
  //   Outputs
  //   Logicas
  //   Comparacion
  //   Extend Selector
  //   Instrucciones de Tipo R
  //   Copia de Registros
  //   Instrucciones de Tipo I
  //   Instrucciones de Tipo J
  //    Salto
  //   Op-Decoder
  //   Especiales
  //   Memoria
  //   Branch Control Selector
  //   Demultiplexer Selector
endmodule

module ALU_Encoder (
  input  ADD,
  input  ADDI,
  input  SUB,
  input  MULT,
  input  MULU,
  input  DIV,
  input  DIVU,
  input  AND,
  input  ANDI,
  input  OR,
  input  ORI,
  input  XOR,
  input  XORI,
  input  NOR,
  input  SLT,
  input  SLTI,
  input  SLTU,
  input  SLTIU,
  output [3:0] ALU_SELECTOR,
  output Type_I
);

  wire ADD_t, AND_t, OR_t, SLT_t, SLTU_t, XOR_t;

  or or_1 (ADD_t, ADD, ADDI);
  or or_2 (AND_t, AND, ANDI);
  or or_3 (OR_t, OR, ORI);
  or or_4 (XOR_t, XOR, XORI);
  or or_5 (SLT_t, SLT, SLTI);
  or or_6 (SLTU_t, SLTU, SLTIU);
  or or_7 (ALU_SELECTOR[3], MULT, MULU, DIV, DIVU);
  or or_8 (ALU_SELECTOR[2], SLT_t, SLTU_t, ADD_t, SUB);
  or or_9 (ALU_SELECTOR[1], NOR, XOR_t, ADD_t, SUB, DIV, DIVU);
  or or_10 (ALU_SELECTOR[0], OR_t, XOR_t, SLTU_t, SUB, MULU, DIVU);
  or or_11 (Type_I, ADDI, ANDI, ORI, XORI, SLTI, SLTIU);

  // Notes on the sheet:
  //   Inputs
  //   ALU Encoder
  //   Outputs
endmodule

module Temp (
  input  [3:0] in_1,
  input  CLK,
  input  Clear,
  output out_4
);

  wire [3:0] counter_1_q;

  Counter #(.width(4), .max('hf)) counter_1 (
    .count(1'b1), .Q(counter_1_q), .clk(CLK), .clr(Clear));  // open: load, D, carry
  Comparator #(.width(4)) comparator_1 (.a(in_1), .b(counter_1_q), .eq(out_4));  // open: gt, lt

  // Notes on the sheet:
  //   Temp
endmodule
